// Logisim project trabalho1.circ as structural Verilog: 13 circuits, main circuit MAIN
module MAIN (
  input  A,
  input  A_2,
  input  A_3,
  input  A_4,
  input  A_5,
  input  A_6,
  input  A_7,
  input  A_8,
  input  B,
  input  B_2,
  input  B_3,
  input  B_4,
  input  B_5,
  input  B_6,
  input  B_7,
  input  B_8,
  input  x,
  input  y,
  input  z,
  output overflow
);

  wire n7_seg_1_a_2, n7_seg_1_b_2, n7_seg_1_c_2, n7_seg_1_d_2, n7_seg_1_e, n7_seg_1_f, n7_seg_1_g,
       n7_seg_2_a_2, n7_seg_2_b_2, n7_seg_2_c_2, n7_seg_2_d_2, n7_seg_2_e, n7_seg_2_f, n7_seg_2_g,
       n7_seg_3_a_2, n7_seg_3_b_2, n7_seg_3_c_2, n7_seg_3_d_2, n7_seg_3_e, n7_seg_3_f, n7_seg_3_g,
       ula_2_cout, ula_3_cout, ula_4_cout, ula_5_cout, ula_6_cout, ula_7_cout, ula_8_cout;
  wire [7:0] divider_1_out, divider_1_rem, divider_2_out, divider_2_rem, ula_8_out_8;

  ULA ula_1 (.Cin(ula_2_cout), .A(A), .B(B), .x(x), .y(y), .z(z), .Cout(overflow), .out_8(ula_8_out_8[7]));
  ULA ula_2 (.Cin(ula_3_cout), .A(A_2), .B(B_2), .x(x), .y(y), .z(z), .Cout(ula_2_cout), .out_8(ula_8_out_8[6]));
  ULA ula_3 (.Cin(ula_4_cout), .A(A_3), .B(B_3), .x(x), .y(y), .z(z), .Cout(ula_3_cout), .out_8(ula_8_out_8[5]));
  Divider divider_1 (.a(ula_8_out_8), .b(8'h64), .out(divider_1_out), .rem(divider_1_rem));  // open: upper
  Divider divider_2 (.a(divider_1_rem), .b(8'ha), .out(divider_2_out), .rem(divider_2_rem));  // open: upper
  ULA ula_4 (.Cin(ula_5_cout), .A(A_4), .B(B_4), .x(x), .y(y), .z(z), .Cout(ula_4_cout), .out_8(ula_8_out_8[4]));
  ULA ula_5 (.Cin(ula_6_cout), .A(A_5), .B(B_5), .x(x), .y(y), .z(z), .Cout(ula_5_cout), .out_8(ula_8_out_8[3]));
  ULA ula_6 (.Cin(ula_7_cout), .A(A_6), .B(B_6), .x(x), .y(y), .z(z), .Cout(ula_6_cout), .out_8(ula_8_out_8[2]));
  _7_seg u_7_seg_1 (
    .A(divider_1_out[0]), .B(divider_1_out[1]), .C(divider_1_out[2]), .D(divider_1_out[3]), .G(n7_seg_1_g),
    .F(n7_seg_1_f), .A_2(n7_seg_1_a_2), .D_2(n7_seg_1_d_2), .C_2(n7_seg_1_c_2), .B_2(n7_seg_1_b_2),
    .E(n7_seg_1_e));
  _7_Segment_Display u_7_segment_display_1 (
    .g(n7_seg_1_g), .f(n7_seg_1_f), .a(n7_seg_1_a_2), .b(n7_seg_1_b_2), .e(n7_seg_1_e), .d(n7_seg_1_d_2),
    .c(n7_seg_1_c_2));  // open: dp
  ULA ula_7 (.Cin(ula_8_cout), .A(A_7), .B(B_7), .x(x), .y(y), .z(z), .Cout(ula_7_cout), .out_8(ula_8_out_8[1]));
  _7_seg u_7_seg_2 (
    .A(divider_2_out[0]), .B(divider_2_out[1]), .C(divider_2_out[2]), .D(divider_2_out[3]), .G(n7_seg_2_g),
    .F(n7_seg_2_f), .A_2(n7_seg_2_a_2), .D_2(n7_seg_2_d_2), .C_2(n7_seg_2_c_2), .B_2(n7_seg_2_b_2),
    .E(n7_seg_2_e));
  _7_Segment_Display u_7_segment_display_2 (
    .g(n7_seg_2_g), .f(n7_seg_2_f), .a(n7_seg_2_a_2), .b(n7_seg_2_b_2), .e(n7_seg_2_e), .d(n7_seg_2_d_2),
    .c(n7_seg_2_c_2));  // open: dp
  ULA ula_8 (.Cin(1'b0), .A(A_8), .B(B_8), .x(x), .y(y), .z(z), .Cout(ula_8_cout), .out_8(ula_8_out_8[0]));
  _7_seg u_7_seg_3 (
    .A(divider_2_rem[0]), .B(divider_2_rem[1]), .C(divider_2_rem[2]), .D(divider_2_rem[3]), .G(n7_seg_3_g),
    .F(n7_seg_3_f), .A_2(n7_seg_3_a_2), .D_2(n7_seg_3_d_2), .C_2(n7_seg_3_c_2), .B_2(n7_seg_3_b_2),
    .E(n7_seg_3_e));
  _7_Segment_Display u_7_segment_display_3 (
    .g(n7_seg_3_g), .f(n7_seg_3_f), .a(n7_seg_3_a_2), .b(n7_seg_3_b_2), .e(n7_seg_3_e), .d(n7_seg_3_d_2),
    .c(n7_seg_3_c_2));  // open: dp

  // Notes on the sheet:
  //   H
  //   G
  //   F
  //   E
  //   D
  //   C
  //   B
  //   A
endmodule

// ULA
module ULA (
  input  Cin,
  input  A,
  input  B,
  input  x,
  input  y,
  input  z,
  output Cout,
  output out_8
);

  wire decoder_1_and, decoder_1_nand, decoder_1_nor, decoder_1_not, decoder_1_or, decoder_1_soma,
       decoder_1_subtracao, decoder_1_xor, mux_1_out_9, operador_1_s;

  decoder decoder_1 (
    .subtracao(decoder_1_subtracao), .soma(decoder_1_soma), .\xor (decoder_1_xor), .\nor (decoder_1_nor),
    .\nand (decoder_1_nand), .\not (decoder_1_not), .\or (decoder_1_or), .\and (decoder_1_and), .x(x), .y(y),
    .z(z));
  operador operador_1 (
    .A(A), .B(B), .subtracao(decoder_1_subtracao), .soma(decoder_1_soma), .S(operador_1_s), .Cout(Cout),
    .Cin(Cin));
  mux mux_1 (
    .\and (decoder_1_and), .\or (decoder_1_or), .\not (decoder_1_not), .\nand (decoder_1_nand),
    .\nor (decoder_1_nor), .\xor (decoder_1_xor), .A(A), .B(B), .out_9(mux_1_out_9));
  or or_1 (out_8, operador_1_s, mux_1_out_9);
endmodule

// decoder
module decoder (
  input  x,
  input  y,
  input  z,
  output subtracao,
  output soma,
  output \xor ,
  output \nor ,
  output \nand ,
  output \not ,
  output \or ,
  output \and 
);

  wire not_1_out, not_2_out, not_3_out;

  not not_1 (not_1_out, x);
  not not_2 (not_2_out, y);
  not not_3 (not_3_out, z);
  and and_1 (subtracao, x, y, z);
  and and_2 (soma, x, y, not_3_out);
  and and_3 (\xor , x, not_2_out, z);
  and and_4 (\nor , x, not_2_out, not_3_out);
  and and_5 (\nand , not_1_out, y, z);
  and and_6 (\not , not_1_out, y, not_3_out);
  and and_7 (\or , not_1_out, not_2_out, z);
  and and_8 (\and , not_1_out, not_2_out, not_3_out);
endmodule

// mux
module mux (
  input  \and ,
  input  \or ,
  input  \not ,
  input  \nand ,
  input  \nor ,
  input  \xor ,
  input  A,
  input  B,
  output out_9
);

  wire and_1_out, and_2_out, and_3_out, and_4_out, and_5_out, and_6_out, and_7_out, nand_1_out, nor_1_out,
       not_1_out, or_1_out, xor_1_out;

  and and_1 (and_1_out, A, B);
  or or_1 (or_1_out, A, B);
  not not_1 (not_1_out, B);
  nand nand_1 (nand_1_out, A, B);
  nor nor_1 (nor_1_out, A, B);
  xor xor_1 (xor_1_out, A, B);
  and and_2 (and_2_out, and_1_out, \and );
  and and_3 (and_3_out, or_1_out, \or );
  and and_4 (and_4_out, not_1_out, \not );
  and and_5 (and_5_out, nand_1_out, \nand );
  and and_6 (and_6_out, nor_1_out, \nor );
  and and_7 (and_7_out, xor_1_out, \xor );
  or or_2 (out_9, and_2_out, and_3_out, and_4_out, and_5_out, and_6_out, and_7_out);
endmodule

// operador
module operador (
  input  Cin,
  input  A,
  input  B,
  input  subtracao,
  input  soma,
  output Cout,
  output S
);

  wire and_1_out, and_2_out, and_3_out, xor_1_out, xor_2_out, xor_3_out, xor_4_out;

  xor xor_1 (xor_1_out, A, subtracao);
  xor xor_2 (xor_2_out, B, Cin);
  and and_1 (and_1_out, Cin, xor_1_out);
  and and_2 (and_2_out, Cin, B);
  and and_3 (and_3_out, xor_1_out, B);
  xor xor_3 (xor_3_out, A, xor_2_out);
  xor xor_4 (xor_4_out, subtracao, soma);
  or or_1 (Cout, and_1_out, and_2_out, and_3_out);
  and and_4 (S, xor_3_out, xor_4_out);
endmodule

// 7 seg
module _7_seg (
  input  D,
  input  C,
  input  B,
  input  A,
  output G,
  output F,
  output A_2,
  output B_2,
  output C_2,
  output D_2,
  output E
);

  G g_1 (.out_5(G), .A(D), .B(C), .C(B), .D(A));
  F f_1 (.out_5(F), .A(D), .B(C), .C(B), .D(A));
  A a_1 (.out_5(A_2), .A(D), .B(C), .C(B), .D(A));
  B b_1 (.out_4(B_2), .B(C), .C(B), .D(A));
  C c_1 (.out_4(C_2), .B(C), .C(B), .D(A));
  D d_1 (.out_5(D_2), .A(D), .B(C), .C(B), .D(A));
  E e_1 (.out_4(E), .B(C), .C(B), .D(A));
endmodule

// A
module A (
  input  A,
  input  B,
  input  C,
  input  D,
  output out_5
);

  wire and_1_out, and_2_out, not_1_out, not_2_out;

  not not_1 (not_1_out, B);
  not not_2 (not_2_out, D);
  and and_1 (and_1_out, B, D);
  and and_2 (and_2_out, not_1_out, not_2_out);
  or or_1 (out_5, A, C, and_1_out, and_2_out);
endmodule

// B
module B (
  input  B,
  input  C,
  input  D,
  output out_4
);

  wire and_1_out, and_2_out, not_1_out, not_2_out, not_3_out;

  not not_1 (not_1_out, B);
  and and_1 (and_1_out, C, D);
  not not_2 (not_2_out, C);
  and and_2 (and_2_out, not_2_out, not_3_out);
  not not_3 (not_3_out, D);
  or or_1 (out_4, not_1_out, and_1_out, and_2_out);
endmodule

// C
module C (
  input  B,
  input  C,
  input  D,
  output out_4
);

  wire not_1_out;

  not not_1 (not_1_out, C);
  or or_1 (out_4, B, not_1_out, D);
endmodule

// D
module D (
  input  A,
  input  B,
  input  C,
  input  D,
  output out_5
);

  wire and_1_out, and_2_out, and_3_out, and_4_out, not_1_out, not_2_out, not_3_out, not_4_out, not_5_out;

  not not_1 (not_1_out, B);
  not not_2 (not_2_out, D);
  not not_3 (not_3_out, B);
  not not_4 (not_4_out, D);
  not not_5 (not_5_out, C);
  and and_1 (and_1_out, not_1_out, not_2_out);
  and and_2 (and_2_out, not_3_out, C);
  and and_3 (and_3_out, C, not_4_out);
  and and_4 (and_4_out, B, not_5_out, D);
  or or_1 (out_5, A, and_1_out, and_2_out, and_3_out, and_4_out);
endmodule

// E
module E (
  input  B,
  input  C,
  input  D,
  output out_4
);

  wire and_1_out, and_2_out, not_1_out, not_2_out, not_3_out;

  not not_1 (not_1_out, B);
  and and_1 (and_1_out, not_1_out, not_2_out);
  not not_2 (not_2_out, D);
  and and_2 (and_2_out, C, not_3_out);
  not not_3 (not_3_out, D);
  or or_1 (out_4, and_1_out, and_2_out);
endmodule

// F
module F (
  input  A,
  input  B,
  input  C,
  input  D,
  output out_5
);

  wire and_1_out, and_2_out, and_3_out, not_1_out, not_2_out, not_3_out, not_4_out;

  not not_1 (not_1_out, C);
  and and_1 (and_1_out, not_1_out, not_2_out);
  not not_2 (not_2_out, D);
  and and_2 (and_2_out, B, not_3_out);
  not not_3 (not_3_out, C);
  and and_3 (and_3_out, B, not_4_out);
  not not_4 (not_4_out, D);
  or or_1 (out_5, A, and_1_out, and_2_out, and_3_out);
endmodule

// G
module G (
  input  A,
  input  B,
  input  C,
  input  D,
  output out_5
);

  wire and_1_out, and_2_out, and_3_out, not_1_out, not_2_out, not_3_out;

  and and_1 (and_1_out, B, not_1_out);
  not not_1 (not_1_out, C);
  not not_2 (not_2_out, B);
  and and_2 (and_2_out, not_2_out, C);
  and and_3 (and_3_out, C, not_3_out);
  not not_3 (not_3_out, D);
  or or_1 (out_5, A, and_1_out, and_2_out, and_3_out);
endmodule
