// Logisim project relogio.circ as structural Verilog: 14 circuits, main circuit _sec
module main (
  input  set_hora,
  input  set_min,
  input  set_sec
);

  wire comp13_1_clear, hora_1__12, hora_1_s0_hora, hora_1_s1_hora, hora_1_s2_hora, hora_1_s3_hora,
       hora_1_s4_hora, hora_1_s5_hora, j_k_ff_1_q, min_1_clk__hora, min_1_s0_min, min_1_s1_min, min_1_s2_min,
       min_1_s3_min, min_1_s4_min, min_1_s5_min, min_1_s6_min, n7_seg_1_a_2, n7_seg_1_b_2, n7_seg_1_c_2,
       n7_seg_1_d_2, n7_seg_1_e, n7_seg_1_f, n7_seg_1_g, n7_seg_2_a_2, n7_seg_2_b_2, n7_seg_2_c_2,
       n7_seg_2_d_2, n7_seg_2_e, n7_seg_2_f, n7_seg_2_g, n7_seg_3_a_2, n7_seg_3_b_2, n7_seg_3_c_2,
       n7_seg_3_d_2, n7_seg_3_e, n7_seg_3_f, n7_seg_3_g, n7_seg_4_a_2, n7_seg_4_b_2, n7_seg_4_c_2,
       n7_seg_4_d_2, n7_seg_4_e, n7_seg_4_f, n7_seg_4_g, n7_seg_5_a_2, n7_seg_5_b_2, n7_seg_5_c_2,
       n7_seg_5_d_2, n7_seg_5_e, n7_seg_5_f, n7_seg_5_g, n7_seg_6_a_2, n7_seg_6_b_2, n7_seg_6_c_2,
       n7_seg_6_d_2, n7_seg_6_e, n7_seg_6_f, n7_seg_6_g, n7_seg_am_pm_1_a, n7_seg_am_pm_1_b,
       n7_seg_am_pm_1_c, n7_seg_am_pm_1_d, n7_seg_am_pm_1_e, n7_seg_am_pm_1_f, n7_seg_am_pm_1_g, or_1_out,
       or_2_out, sec_1_clk_min, sec_1_s0_sec, sec_1_s1_sec, sec_1_s2_sec, sec_1_s3_sec, sec_1_s4_sec,
       sec_1_s5_sec, sec_1_s6_sec;

  comp13 comp13_1 (.parametro(hora_1__12), .clear(comp13_1_clear));
  _7_seg u_7_seg_1 (
    .C(1'b0), .B(hora_1_s5_hora), .A(hora_1_s4_hora), .G(n7_seg_1_g), .F(n7_seg_1_f), .A_2(n7_seg_1_a_2),
    .B_2(n7_seg_1_b_2), .C_2(n7_seg_1_c_2), .D_2(n7_seg_1_d_2), .E(n7_seg_1_e), .D(1'b0));
  _7_Segment_Display u_7_segment_display_1 (
    .g(n7_seg_1_g), .f(n7_seg_1_f), .a(n7_seg_1_a_2), .b(n7_seg_1_b_2), .e(n7_seg_1_e), .d(n7_seg_1_d_2),
    .c(n7_seg_1_c_2));  // open: dp
  _7_seg u_7_seg_2 (
    .C(hora_1_s2_hora), .B(hora_1_s1_hora), .A(hora_1_s0_hora), .G(n7_seg_2_g), .F(n7_seg_2_f),
    .A_2(n7_seg_2_a_2), .B_2(n7_seg_2_b_2), .C_2(n7_seg_2_c_2), .D_2(n7_seg_2_d_2), .E(n7_seg_2_e),
    .D(hora_1_s3_hora));
  _7_Segment_Display u_7_segment_display_2 (
    .g(n7_seg_2_g), .f(n7_seg_2_f), .a(n7_seg_2_a_2), .b(n7_seg_2_b_2), .e(n7_seg_2_e), .d(n7_seg_2_d_2),
    .c(n7_seg_2_c_2));  // open: dp
  hora hora_1 (
    .CLK(or_1_out), .s4_hora(hora_1_s4_hora), .s2_hora(hora_1_s2_hora), .s3_hora(hora_1_s3_hora),
    .s1_hora(hora_1_s1_hora), .s0_hora(hora_1_s0_hora), ._12(hora_1__12), .CLEAR(comp13_1_clear),
    .s5_hora(hora_1_s5_hora));
  or or_1 (or_1_out, set_hora, min_1_clk__hora);
  _7_seg u_7_seg_3 (
    .C(min_1_s6_min), .B(min_1_s5_min), .A(min_1_s4_min), .G(n7_seg_3_g), .F(n7_seg_3_f), .A_2(n7_seg_3_a_2),
    .B_2(n7_seg_3_b_2), .C_2(n7_seg_3_c_2), .D_2(n7_seg_3_d_2), .E(n7_seg_3_e), .D(1'b0));
  _7_Segment_Display u_7_segment_display_3 (
    .g(n7_seg_3_g), .f(n7_seg_3_f), .a(n7_seg_3_a_2), .b(n7_seg_3_b_2), .e(n7_seg_3_e), .d(n7_seg_3_d_2),
    .c(n7_seg_3_c_2));  // open: dp
  min min_1 (
    .CLK(or_2_out), .s6_min(min_1_s6_min), .s5_min(min_1_s5_min), .s4_min(min_1_s4_min),
    .s3_min(min_1_s3_min), .s2_min(min_1_s2_min), .s1_min(min_1_s1_min), .s0_min(min_1_s0_min),
    .CLK__hora(min_1_clk__hora));
  or or_2 (or_2_out, set_min, sec_1_clk_min);
  _7_seg u_7_seg_4 (
    .C(min_1_s2_min), .B(min_1_s1_min), .A(min_1_s0_min), .G(n7_seg_4_g), .F(n7_seg_4_f), .A_2(n7_seg_4_a_2),
    .B_2(n7_seg_4_b_2), .C_2(n7_seg_4_c_2), .D_2(n7_seg_4_d_2), .E(n7_seg_4_e), .D(min_1_s3_min));
  _7_Segment_Display u_7_segment_display_4 (
    .g(n7_seg_4_g), .f(n7_seg_4_f), .a(n7_seg_4_a_2), .b(n7_seg_4_b_2), .e(n7_seg_4_e), .d(n7_seg_4_d_2),
    .c(n7_seg_4_c_2));  // open: dp
  _7_seg u_7_seg_5 (
    .C(sec_1_s6_sec), .B(sec_1_s5_sec), .A(sec_1_s4_sec), .G(n7_seg_5_g), .F(n7_seg_5_f), .A_2(n7_seg_5_a_2),
    .B_2(n7_seg_5_b_2), .C_2(n7_seg_5_c_2), .D_2(n7_seg_5_d_2), .E(n7_seg_5_e));  // open: D
  _7_Segment_Display u_7_segment_display_5 (
    .g(n7_seg_5_g), .f(n7_seg_5_f), .a(n7_seg_5_a_2), .b(n7_seg_5_b_2), .e(n7_seg_5_e), .d(n7_seg_5_d_2),
    .c(n7_seg_5_c_2));  // open: dp
  sec sec_1 (
    .s0_sec(sec_1_s0_sec), .s1_sec(sec_1_s1_sec), .s2_sec(sec_1_s2_sec), .s3_sec(sec_1_s3_sec),
    .s4_sec(sec_1_s4_sec), .s5_sec(sec_1_s5_sec), .s6_sec(sec_1_s6_sec), .CLK_min(sec_1_clk_min),
    .in_1(set_sec));
  _7_seg u_7_seg_6 (
    .C(sec_1_s2_sec), .B(sec_1_s1_sec), .A(sec_1_s0_sec), .G(n7_seg_6_g), .F(n7_seg_6_f), .A_2(n7_seg_6_a_2),
    .B_2(n7_seg_6_b_2), .C_2(n7_seg_6_c_2), .D_2(n7_seg_6_d_2), .E(n7_seg_6_e), .D(sec_1_s3_sec));
  _7_Segment_Display u_7_segment_display_6 (
    .g(n7_seg_6_g), .f(n7_seg_6_f), .a(n7_seg_6_a_2), .b(n7_seg_6_b_2), .e(n7_seg_6_e), .d(n7_seg_6_d_2),
    .c(n7_seg_6_c_2));  // open: dp
  J_K_Flip_Flop j_k_ff_1 (
    .J(1'b1), .clk(comp13_1_clear), .K(1'b1), .Q(j_k_ff_1_q), .en(1'b1));  // open: Qn, preset, reset
  _7_Segment_Display u_7_segment_display_7 (
    .g(n7_seg_am_pm_1_g), .f(n7_seg_am_pm_1_f), .a(n7_seg_am_pm_1_a), .b(n7_seg_am_pm_1_b),
    .e(n7_seg_am_pm_1_e), .d(n7_seg_am_pm_1_d), .c(n7_seg_am_pm_1_c));  // open: dp
  _7_seg__am_pm u_7_seg_am_pm_1 (
    .set(j_k_ff_1_q), .G(n7_seg_am_pm_1_g), .F(n7_seg_am_pm_1_f), .A(n7_seg_am_pm_1_a), .B(n7_seg_am_pm_1_b),
    .C(n7_seg_am_pm_1_c), .D(n7_seg_am_pm_1_d), .E(n7_seg_am_pm_1_e));
  _7_Segment_Display u_7_segment_display_8 (.g(1'b1), .a(1'b1), .e(1'b1), .c(1'b1));  // open: f, b, d, dp

  // Notes on the sheet:
  //   Para evitar bugs, deve-se começar a setar o horário nessa ordem:
  //   hora ->minuto->segundo
  //   Além de deixar apenas o set dos segundos em 1 
endmodule

// SEGUNDOS
module sec (
  input  in_1,
  output CLK_min,
  output s6_sec,
  output s5_sec,
  output s4_sec,
  output s3_sec,
  output s2_sec,
  output s1_sec,
  output s0_sec
);

  wire and_1_out, and_2_out, and_3_out, and_4_out, and_5_out, and_6_out, clock_1_out, ff3_qn, ff6_qn,
       not_1_out, not_2_out;

  Clock clock_1 (.out(clock_1_out));
  not not_1 (not_1_out, clock_1_out);
  and and_1 (and_1_out, in_1, not_1_out);
  J_K_Flip_Flop ff0 (
    .J(1'b1), .clk(and_1_out), .K(1'b1), .Q(s0_sec), .preset(1'b0), .en(1'b1), .reset(1'b0));  // open: Qn
  and and_2 (and_2_out, ff3_qn, s0_sec);
  J_K_Flip_Flop ff1 (
    .J(and_2_out), .clk(and_1_out), .K(s0_sec), .Q(s1_sec), .preset(1'b0), .en(1'b1), .reset(1'b0));  // open: Qn
  and and_3 (and_3_out, s0_sec, s1_sec);
  J_K_Flip_Flop ff2 (
    .J(and_3_out), .clk(and_1_out), .K(and_3_out), .Q(s2_sec), .preset(1'b0), .en(1'b1), .reset(1'b0));  // open: Qn
  J_K_Flip_Flop ff3 (
    .J(and_4_out), .clk(and_1_out), .K(s0_sec), .Q(s3_sec), .Qn(ff3_qn), .preset(1'b0), .en(1'b1),
    .reset(1'b0));
  and and_4 (and_4_out, and_3_out, s2_sec);
  not not_2 (not_2_out, s3_sec);
  J_K_Flip_Flop ff4 (
    .J(1'b1), .clk(not_2_out), .K(1'b1), .Q(s4_sec), .preset(1'b0), .en(1'b1), .reset(1'b0));  // open: Qn
  and and_5 (and_5_out, ff6_qn, s4_sec);
  J_K_Flip_Flop ff5 (
    .J(and_5_out), .clk(not_2_out), .K(s4_sec), .Q(s5_sec), .preset(1'b0), .en(1'b1), .reset(1'b0));  // open: Qn
  and and_6 (and_6_out, s4_sec, s5_sec);
  J_K_Flip_Flop ff6 (
    .J(and_6_out), .clk(not_2_out), .K(s4_sec), .Q(CLK_min), .Qn(ff6_qn), .preset(1'b0), .en(1'b1),
    .reset(1'b0));

  assign s6_sec = CLK_min;

  // Notes on the sheet:
  //   DEZENA
  //   UNIDADE
endmodule

// MINUTOS
module min (
  input  CLK,
  output CLK__hora,
  output s6_min,
  output s5_min,
  output s4_min,
  output s3_min,
  output s2_min,
  output s1_min,
  output s0_min
);

  wire and_1_out, and_2_out, and_3_out, and_4_out, and_5_out, ff3_qn, ff6_qn, not_1_out, not_2_out;

  not not_1 (not_1_out, CLK);
  J_K_Flip_Flop ff0 (
    .J(1'b1), .clk(not_1_out), .K(1'b1), .Q(s0_min), .preset(1'b0), .en(1'b1), .reset(1'b0));  // open: Qn
  and and_1 (and_1_out, ff3_qn, s0_min);
  J_K_Flip_Flop ff1 (
    .J(and_1_out), .clk(not_1_out), .K(s0_min), .Q(s1_min), .preset(1'b0), .en(1'b1), .reset(1'b0));  // open: Qn
  and and_2 (and_2_out, s0_min, s1_min);
  J_K_Flip_Flop ff2 (
    .J(and_2_out), .clk(not_1_out), .K(and_2_out), .Q(s2_min), .preset(1'b0), .en(1'b1), .reset(1'b0));  // open: Qn
  and and_3 (and_3_out, and_2_out, s2_min);
  J_K_Flip_Flop ff3 (
    .J(and_3_out), .clk(not_1_out), .K(s0_min), .Q(s3_min), .Qn(ff3_qn), .preset(1'b0), .en(1'b1),
    .reset(1'b0));
  not not_2 (not_2_out, s3_min);
  J_K_Flip_Flop ff4 (
    .J(1'b1), .clk(not_2_out), .K(1'b1), .Q(s4_min), .preset(1'b0), .en(1'b1), .reset(1'b0));  // open: Qn
  and and_4 (and_4_out, ff6_qn, s4_min);
  and and_5 (and_5_out, s4_min, s5_min);
  J_K_Flip_Flop ff5 (
    .J(and_4_out), .clk(not_2_out), .K(s4_min), .Q(s5_min), .preset(1'b0), .en(1'b1), .reset(1'b0));  // open: Qn
  J_K_Flip_Flop ff6 (
    .J(and_5_out), .clk(not_2_out), .K(s4_min), .Q(CLK__hora), .Qn(ff6_qn), .preset(1'b0), .en(1'b1),
    .reset(1'b0));

  assign s6_min = CLK__hora;

  // Notes on the sheet:
  //   DEZENA
  //   UNIDADE
endmodule

// HORAS
module hora (
  input  CLK,
  input  CLEAR,
  output s5_hora,
  output s4_hora,
  output s3_hora,
  output s2_hora,
  output s1_hora,
  output s0_hora,
  output _12
);

  wire and_1_out, and_2_out, and_3_out, and_4_out, and_5_out, and_6_out, and_7_out, and_8_out, FF_0_qn,
       FF_1_qn, FF_3_qn, FF_4_qn, not_1_out, not_2_out, or_1_out;

  not not_1 (not_1_out, CLK);
  or or_1 (or_1_out, CLEAR, and_1_out);
  and and_1 (and_1_out, FF_0_qn, and_3_out);
  J_K_Flip_Flop FF_0 (
    .J(1'b1), .clk(not_1_out), .K(1'b1), .Q(s0_hora), .Qn(FF_0_qn), .preset(or_1_out), .en(1'b1), .reset(1'b0));
  and and_2 (and_2_out, FF_3_qn, s0_hora);
  J_K_Flip_Flop FF_1 (
    .J(and_2_out), .clk(not_1_out), .K(s0_hora), .Q(s1_hora), .Qn(FF_1_qn), .preset(1'b0), .en(1'b1),
    .reset(or_1_out));
  and and_3 (and_3_out, FF_1_qn, and_5_out);
  and and_4 (and_4_out, s0_hora, s1_hora);
  J_K_Flip_Flop FF_2 (
    .J(and_4_out), .clk(not_1_out), .K(and_4_out), .Q(s2_hora), .preset(1'b0), .en(1'b1), .reset(or_1_out));  // open: Qn
  and and_5 (and_5_out, s2_hora, and_7_out);
  and and_6 (and_6_out, and_4_out, s2_hora);
  and and_7 (and_7_out, FF_3_qn, and_8_out);
  J_K_Flip_Flop FF_3 (
    .J(and_6_out), .clk(not_1_out), .K(s0_hora), .Q(s3_hora), .Qn(FF_3_qn), .preset(1'b0), .en(1'b1),
    .reset(or_1_out));
  not not_2 (not_2_out, s3_hora);
  and and_8 (and_8_out, FF_4_qn, s5_hora);
  J_K_Flip_Flop FF_4 (
    .J(1'b1), .clk(not_2_out), .K(1'b1), .Q(s4_hora), .Qn(FF_4_qn), .preset(1'b0), .en(1'b1), .reset(or_1_out));
  J_K_Flip_Flop FF_5 (
    .J(s4_hora), .clk(not_2_out), .K(s4_hora), .Q(s5_hora), .preset(1'b0), .en(1'b1), .reset(or_1_out));  // open: Qn
  and and_9 (_12, s0_hora, s1_hora, s4_hora);

  // Notes on the sheet:
  //   DEZENA
  //   UNIDADE
endmodule

// 7 SEG
module _7_seg (
  input  D,
  input  C,
  input  B,
  input  A,
  output G,
  output F,
  output A_2,
  output B_2,
  output C_2,
  output D_2,
  output E
);

  G g_1 (.out_5(G), .A(D), .B(C), .C(B), .D(A));
  F f_1 (.out_5(F), .A(D), .B(C), .C(B), .D(A));
  A a_1 (.out_5(A_2), .A(D), .B(C), .C(B), .D(A));
  C c_1 (.out_4(C_2), .B(C), .C(B), .D(A));
  B b_1 (.out_4(B_2), .B(C), .C(B), .D(A));
  D d_1 (.out_5(D_2), .A(D), .B(C), .C(B), .D(A));
  E e_1 (.out_4(E), .B(C), .C(B), .D(A));
endmodule

// A
module A (
  input  A,
  input  B,
  input  C,
  input  D,
  output out_5
);

  wire and_1_out, and_2_out, not_1_out, not_2_out;

  not not_1 (not_1_out, B);
  not not_2 (not_2_out, D);
  and and_1 (and_1_out, B, D);
  and and_2 (and_2_out, not_1_out, not_2_out);
  or or_1 (out_5, A, C, and_1_out, and_2_out);
endmodule

// B
module B (
  input  B,
  input  C,
  input  D,
  output out_4
);

  wire and_1_out, and_2_out, not_1_out, not_2_out, not_3_out;

  not not_1 (not_1_out, B);
  and and_1 (and_1_out, C, D);
  not not_2 (not_2_out, C);
  and and_2 (and_2_out, not_2_out, not_3_out);
  not not_3 (not_3_out, D);
  or or_1 (out_4, not_1_out, and_1_out, and_2_out);
endmodule

module C (
  input  B,
  input  C,
  input  D,
  output out_4
);

  wire not_1_out;

  not not_1 (not_1_out, C);
  or or_1 (out_4, B, not_1_out, D);
endmodule

// D
module D (
  input  A,
  input  B,
  input  C,
  input  D,
  output out_5
);

  wire and_1_out, and_2_out, and_3_out, and_4_out, not_1_out, not_2_out, not_3_out, not_4_out, not_5_out;

  not not_1 (not_1_out, B);
  not not_2 (not_2_out, D);
  not not_3 (not_3_out, B);
  not not_4 (not_4_out, D);
  not not_5 (not_5_out, C);
  and and_1 (and_1_out, not_1_out, not_2_out);
  and and_2 (and_2_out, not_3_out, C);
  and and_3 (and_3_out, C, not_4_out);
  and and_4 (and_4_out, B, not_5_out, D);
  or or_1 (out_5, A, and_1_out, and_2_out, and_3_out, and_4_out);
endmodule

// E
module E (
  input  B,
  input  C,
  input  D,
  output out_4
);

  wire and_1_out, and_2_out, not_1_out, not_2_out, not_3_out;

  not not_1 (not_1_out, B);
  and and_1 (and_1_out, not_1_out, not_2_out);
  not not_2 (not_2_out, D);
  and and_2 (and_2_out, C, not_3_out);
  not not_3 (not_3_out, D);
  or or_1 (out_4, and_1_out, and_2_out);
endmodule

// F
module F (
  input  A,
  input  B,
  input  C,
  input  D,
  output out_5
);

  wire and_1_out, and_2_out, and_3_out, not_1_out, not_2_out, not_3_out, not_4_out;

  not not_1 (not_1_out, C);
  and and_1 (and_1_out, not_1_out, not_2_out);
  not not_2 (not_2_out, D);
  and and_2 (and_2_out, B, not_3_out);
  not not_3 (not_3_out, C);
  and and_3 (and_3_out, B, not_4_out);
  not not_4 (not_4_out, D);
  or or_1 (out_5, A, and_1_out, and_2_out, and_3_out);
endmodule

// G
module G (
  input  A,
  input  B,
  input  C,
  input  D,
  output out_5
);

  wire and_1_out, and_2_out, and_3_out, not_1_out, not_2_out, not_3_out;

  and and_1 (and_1_out, B, not_1_out);
  not not_1 (not_1_out, C);
  not not_2 (not_2_out, B);
  and and_2 (and_2_out, not_2_out, C);
  and and_3 (and_3_out, C, not_3_out);
  not not_3 (not_3_out, D);
  or or_1 (out_5, A, and_1_out, and_2_out, and_3_out);
endmodule

// 7 SEG AM/PM
module _7_seg__am_pm (
  input  set,
  output G,
  output F,
  output A,
  output B,
  output C,
  output D,
  output E
);

  not not_1 (C, set);

  assign A = 1'b1;
  assign B = 1'b1;
  assign D = 1'b0;
  assign E = 1'b1;
  assign F = 1'b1;
  assign G = 1'b1;
endmodule

module comp13 (
  input  parametro,
  output clear
);

  wire comparator_2_eq;
  wire [3:3] comparator_1_eq;

  Comparator #(.width(1), .mode("unsigned")) comparator_1 (
    .a(parametro), .b(1'b1), .eq(comparator_1_eq[3]));  // open: gt, lt
  Comparator #(.width(7), .mode("unsigned")) comparator_2 (
    .a(7'b0001101), .b({3'b000, {2{comparator_1_eq[3]}}, 1'b0, comparator_1_eq[3]}), .eq(comparator_2_eq));  // open: gt, lt
  and and_1 (clear, comparator_2_eq, 1'b1);
endmodule
